# Fritzing sketch 036-esempio-diodo (saved by Fritzing 0.9.0b)
breadboards: 1

parts:
  D1 = Rectifier Diode [part_number=1N4001 package="300 mil [THT]"]
  R1 = Resistor [tolerance=±5% resistance=390 package=THT]
  LED1 = LED - 5mm [color="Red (633nm)" package="5 mm [THT]"]

nets:
  N1: D1.cathode, R1.Pin_0
  N2: R1.Pin_1, LED1.anode
