# Fritzing sketch raddrizzatore-semionda (saved by Fritzing 0.9.0b)
breadboards: 1

parts:
  D1 = Rectifier Diode [part_number=1N4001 package="300 mil [THT]"]
  R1 = Resistor [tolerance=±5% resistance=1k package=THT]

nets:
  N1: D1.cathode, R1.Pin_1
