# Fritzing sketch millefori (saved by Fritzing 0.9.0b)
perfboards: 1

parts:
  R1 = Resistor [tolerance=±5% resistance=390 package=THT]
  LED1 = LED - 5mm [color="Red (633nm)" package="5 mm [THT]"]
  S1 = Pushbutton [package="[THT]"]
  VCC1 = Battery

nets:
  N1: R1.Pin_0, S1.Pin_1, S1.Pin_2
  N2: R1.Pin_1, LED1.anode
  N3: LED1.cathode, VCC1.-
  N4: S1.Pin_3, S1.Pin_4, VCC1.+
