# Fritzing sketch bjt-fotores-led_bb (saved by Fritzing 0.9.0b)
breadboards: 1

parts:
  Q1 = NPN-Transistor [package="TO92 [THT]"]
  R1 = Resistor [tolerance=±5% resistance=390 package=THT]
  LED1 = LED - 5mm [color="Red (633nm)" package="5 mm [THT]"]
  R2 = Resistor [tolerance=±5% resistance=1k package=THT]
  R3 = Photocell (LDR) [package=THT]
  R4 = Trimmer Potentiometer [maximum_resistance=10kΩ package=THT]
  VCC1 = Battery

nets:
  N1: Q1.E, R3.pin_0, VCC1.-
  N2: Q1.B, R2.Pin_0, R3.pin_1
  N3: Q1.C, R1.Pin_0
  N4: R1.Pin_1, LED1.cathode
  N5: LED1.anode, R4.wiper, VCC1.+
  N6: R2.Pin_1, R4.leg1
