# Fritzing sketch bjt_e_rele (saved by Fritzing 0.9.0b)
breadboards: 1

parts:
  Q1 = NPN-Transistor [package="TO92 [THT]"]
  D1 = Rectifier Diode [part_number=1N4001 package="300 mil [THT]"]
  R1 = Resistor [tolerance=±5% resistance=390 package=THT]
  S1 = Pushbutton [package="[THT]"]
  R2 = Resistor [tolerance=±5% resistance=1k package=THT]
  LED1 = LED - 5mm [color="Red (633nm)" package="5 mm [THT]"]
  K1 = Relay [part_number=FRS1B-S package=THT]

nets:
  N1: Q1.B, S1.Pin_1, S1.Pin_2
  N2: Q1.C, D1.anode, R1.Pin_0, K1.COIL2
  N3: D1.cathode, K1.COIL1
  N4: R1.Pin_1, LED1.cathode
  N5: S1.Pin_3, S1.Pin_4, R2.Pin_0
  N6: R2.Pin_1, LED1.anode
  N7: K1.C1, K1.C2
