# Fritzing sketch ecomune (saved by Fritzing 0.9.0b)
breadboards: 1

parts:
  Q1 = NPN-Transistor [package="TO92 [THT]"]
  R1 = Resistor [tolerance=±5% resistance=10k package=THT]
  R2 = Resistor [tolerance=±5% resistance=1k package=THT]
  R3 = Resistor [tolerance=±5% resistance=100k package=THT]
  R4 = Resistor [tolerance=±5% resistance=12k package=THT]
  C1 = Electrolytic Capacitor [capacitance=1µF package="100 mil [THT, electrolytic]"]
  C2 = Electrolytic Capacitor [capacitance=1µF package="100 mil [THT, electrolytic]"]

nets:
  N1: Q1.E, R2.Pin_1
  N2: Q1.B, R3.Pin_1, R4.Pin_0, C1.+
  N3: Q1.C, R1.Pin_0, C2.+
  N4: R1.Pin_1, R3.Pin_0
  N5: R2.Pin_0, R4.Pin_1
