# Fritzing sketch led-indicatore-i (saved by Fritzing 0.9.3b)
breadboards: 1

parts:
  Q1 = pnp-Powertransistor [package="TO220 [THT]"]
  R1 = Resistor [tolerance=±5% resistance=10 package=THT]
  R2 = Resistor [tolerance=±5% resistance=390 package=THT]
  LED1 = LED - 5mm [color="Red (633nm)" package="5 mm [THT]"]

nets:
  N1: Q1.base, R1.Pin_1
  N2: Q1.collector, R2.Pin_0
  N3: Q1.emitter, R1.Pin_0
  N4: R2.Pin_1, LED1.anode
