# Fritzing sketch mosfet (saved by Fritzing 0.9.3b)
breadboards: 1

parts:
  Q2 = Basic FET N-Channel [package="TO220 [THT]"]
  R1 = Trimmer Potentiometer [maximum_resistance=10kΩ package=THT]
  R2 = Resistor [tolerance=±5% resistance=390 package=THT]
  LED1 = LED - 5mm [color="Red (633nm)" package="5 mm [THT]"]

nets:
  N1: Q2.gate, R1.leg1
  N2: Q2.drain, R1.wiper
  N3: Q2.source, R2.Pin_0
  N4: R1.leg2, LED1.cathode
  N5: R2.Pin_1, LED1.anode
