# Fritzing sketch mosfet (saved by Fritzing 0.9.3b)
breadboards: 1

parts:
  R1 = Trimmer Potentiometer [maximum_resistance=10kΩ package=THT]
  R2 = Resistor [tolerance=±5% resistance=390 package=THT]
  LED1 = LED - 5mm [color="Red (633nm)" package="5 mm [THT]"]
  Q2 = Basic FET N-Channel [package="TO220 [THT]"]
  D1 = Rectifier Diode [part_number=1N4001 package="300 mil [THT]"]

nets:
  N1: R1.leg1, D1.anode
  N2: R1.wiper, Q2.drain
  N3: R1.leg2, LED1.cathode
  N4: R2.Pin_0, Q2.source
  N5: R2.Pin_1, LED1.anode
  N6: Q2.gate, D1.cathode
